# Fritzing sketch thermometer (saved by Fritzing 1.0.4)
breadboards: 1

parts:
  R2 = 12mm Trimmer Potentiometer (Large) [maximum_resistance=10kΩ knob_status=50% power=0.5W package=THT]
  LCD1 = LCD screen
  R3 = Temperature Sensor (Thermistor) [thermistor_type=NTC package=THT]
  R4 = Resistor [tolerance=±5% resistance=10k package="2010 [SMD]"]
  DHT1 = DHT11 Humitidy and Temperature Sensor (3 pins)
  Part1 = Arduino Mega 2560 (Rev3)
  WeMos_D1_Mini1 = WeMos D1 Mini  # not connected

nets:
  VDD: R2.leg1, LCD1.VDD, LCD1.LED+, R3.pin_1, DHT1.Signal, Part1.5V
  N1: R2.wiper, LCD1.V0
  GND: R2.leg2, LCD1.VSS, LCD1.R/W, LCD1.LED-, R4.Pin_1, DHT1.Gnd, Part1.GND
  N2: LCD1.DB4, Part1.D9_PWM
  N3: R3.pin_0, R4.Pin_0, Part1.A0
  N4: DHT1.Plus, Part1.D6_PWM

custom parts:
  DHT11 Humitidy and Temperature Sensor (3 pins): DHT11 Humidity and Temperature Sensor (3 pins).
