# Fritzing sketch themometer (saved by Fritzing 1.0.4)
breadboards: 1

parts:
  R2 = 12mm Trimmer Potentiometer (Large) [maximum_resistance=10kΩ knob_status=50% power=0.5W package=THT]
  LCD1 = LCD screen
  Part1 = Arduino Uno (Rev3)
  R3 = Temperature Sensor (Thermistor) [thermistor_type=NTC package=THT]
  R4 = Resistor [tolerance=±5% resistance=10k package="2010 [SMD]"]
  DHT1 = DHT11 Humitidy and Temperature Sensor (3 pins)

nets:
  VDD: R2.leg1, LCD1.VDD, LCD1.LED+, Part1.5V, R3.pin_1, DHT1.Signal
  N1: R2.wiper, LCD1.V0
  GND: R2.leg2, LCD1.VSS, LCD1.R/W, LCD1.LED-, Part1.GND, R4.Pin_1, DHT1.Gnd
  N2: LCD1.RS, Part1.D7
  N3: LCD1.E, Part1.D8
  N4: LCD1.DB4, Part1.D9_PWM
  N5: LCD1.DB5, Part1.D10_PWM/SS
  N6: LCD1.DB6, Part1.D11_PWM/MOSI
  N7: LCD1.DB7, Part1.D12/MISO
  N8: Part1.A0, R3.pin_0, R4.Pin_0
  N9: Part1.D6_PWM, DHT1.Plus

custom parts:
  DHT11 Humitidy and Temperature Sensor (3 pins): DHT11 Humidity and Temperature Sensor (3 pins).
