# Fritzing sketch thermometer_wifi_screenless_E (saved by Fritzing 1.0.4)
breadboards: 1

parts:
  Part1 = Arduino Nano (Rev3.0)
  WeMos_D1_Mini1 = WeMos D1 Mini  # not connected
  DHT1 = DHT11 Humitidy and Temperature Sensor (3 pins)
  R1 = Resistor [tolerance=±5% resistance=10k package="0402 [SMD]"]
  R2 = Temperature Sensor (Thermistor) [thermistor_type=NTC package=THT]
  R3 = Resistor [tolerance=±5% resistance=10k package="0402 [SMD]"]
  R4 = Temperature Sensor (Thermistor) [thermistor_type=NTC package=THT]
  R5 = Resistor [tolerance=±5% resistance=10k package="0402 [SMD]"]
  R6 = Temperature Sensor (Thermistor) [thermistor_type=NTC package=THT]
  R7 = Resistor [tolerance=±5% resistance=10k package="0402 [SMD]"]
  R8 = Temperature Sensor (Thermistor) [thermistor_type=NTC package=THT]
  LED3 = smd LED [color="Green (555nm)" package="1206 [SMD]"]
  R18 = Resistor [tolerance=±5% resistance=4.7k package="0402 [SMD]"]
  LED4 = smd LED [color="Blue (470nm)" package="1206 [SMD]"]
  R19 = Resistor [tolerance=±5% resistance=4.7k package="0402 [SMD]"]

nets:
  GND: Part1.GND, DHT1.Gnd, R1.Pin_0, R3.Pin_0, R5.Pin_0, R7.Pin_0, LED3.cathode, LED4.cathode
  N1: Part1.D2, R19.Pin_0
  N2: Part1.D3, R18.Pin_0
  N3: Part1.D6, DHT1.Plus
  N4: Part1.5V, DHT1.Signal, R2.pin_1, R4.pin_1, R6.pin_1, R8.pin_1
  N5: Part1.A3, R7.Pin_1, R8.pin_0
  N6: Part1.A2, R5.Pin_1, R6.pin_0
  N7: Part1.A1, R3.Pin_1, R4.pin_0
  N8: Part1.A0, R1.Pin_1, R2.pin_0
  N9: LED3.anode, R19.Pin_1
  N10: R18.Pin_1, LED4.anode

custom parts:
  DHT11 Humitidy and Temperature Sensor (3 pins): DHT11 Humidity and Temperature Sensor (3 pins).
